# Fritzing sketch Circuit (saved by Fritzing 0.8.7b)
breadboards: 1

parts:
  Nokia_5110_LCD_Module1 = Nokia 5110 LCD
  Eleman1 = Arduino Uno (Rev3)
  LED1 = LED - 5mm [color="Blue (470nm)" package="5 mm [THT]"]
  LED2 = LED - 5mm [color="Red (633nm)" package="5 mm [THT]"]
  S1 = Pushbutton [package="[THT]"]
  S2 = Pushbutton [package="[THT]"]
  R1 = Resistor [tolerance=±5% resistance=220 package=THT]
  R2 = Resistor [tolerance=±5% resistance=220 package=THT]
  R3 = Resistor [tolerance=±5% resistance=220 package=THT]
  R4 = Resistor [tolerance=±5% resistance=220 package=THT]
  R5 = Resistor [tolerance=±5% resistance=220 package=THT]
  R6 = Resistor [tolerance=±5% resistance=220 package=THT]
  R7 = Resistor [tolerance=±5% resistance=220 package=THT]
  R8 = Resistor [tolerance=±5% resistance=220 package=THT]
  R9 = Resistor [tolerance=±5% resistance=220 package=THT]
  R10 = Resistor [tolerance=±5% resistance=220 package=THT]
  J1 = Piezo Speaker

nets:
  N1: Nokia_5110_LCD_Module1.VCC, R10.Pin_0
  N2: Nokia_5110_LCD_Module1.GND, R9.Pin_0
  N3: Nokia_5110_LCD_Module1.SCE, R8.Pin_0
  N4: Nokia_5110_LCD_Module1.RST, R7.Pin_0
  N5: Nokia_5110_LCD_Module1.D/C, R6.Pin_0
  N6: Nokia_5110_LCD_Module1.DN(MOSI), Nokia_5110_LCD_Module1.DN(MODI)_(out), S1.Pin_3, S1.Pin_4, R5.Pin_1
  N7: Nokia_5110_LCD_Module1.SCLK, R5.Pin_0
  N8: Nokia_5110_LCD_Module1.LED, Nokia_5110_LCD_Module1.LED_(out), Eleman1.GND, R2.Pin_1, R3.Pin_1, R4.Pin_0
  N9: Eleman1.D8, S2.Pin_1, S2.Pin_2, R3.Pin_0
  N10: Eleman1.D9_PWM, S1.Pin_1, S1.Pin_2, R2.Pin_0
  N11: Eleman1.D10_PWM/SS, LED2.anode
  N12: Eleman1.D11_PWM/MOSI, LED1.anode
  N13: Eleman1.D12/MISO, J1.pin2
  N14: Eleman1.D3_PWM, R10.Pin_1
  N15: Eleman1.D4, R9.Pin_1
  N16: Eleman1.D5_PWM, R8.Pin_1
  N17: Eleman1.D6_PWM, R7.Pin_1
  N18: Eleman1.D7, R6.Pin_1
  N19: Eleman1.5V, S2.Pin_3, S2.Pin_4
  N20: LED1.cathode, R1.Pin_1
  N21: LED2.cathode, R4.Pin_1
  N22: R1.Pin_0, J1.pin1

custom parts:
  Nokia 5110 LCD: Nokia 5110 Graphic 84*48 LCD module such as the Sparkfun LCD-10168 or the clones from Ebay. There is example code for the Arduino available from the Sparkfun site in https://learn.sparkfun.com/tutorials/graphic-lcd-hookup-guide This is a 3.3V device, if you are running it from a 5V micro you need a 5V tolorant level translator such as the 74ahc367 to protect the signal imputs. Rafa G. did a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
